# Fritzing sketch buzgame beta 1 (saved by Fritzing 0.9.9b)
breadboards: 1

parts:
  R1 = Resistor [tolerance=±5% power=0.25 resistance=10k package=THT]
  R2 = Resistor [tolerance=±5% power=0.25 resistance=220 package=THT]
  LED1 = LED - 5mm [color="Red (633nm)" current=0.030 package="5 mm [THT]"]
  J1 = Piezo Speaker
  Mod1 = deneyap kart
  ANT1 = Antenna  # not connected
  ANT2 = Antenna

nets:
  N1: R1.Pin_0, Mod1.pin_12, ANT2.antenna_lead
  N2: R1.Pin_1, LED1.cathode, J1.pin1, Mod1.pin_16, Mod1.pin_17, Mod1.pin_32
  N3: R2.Pin_0, Mod1.pin_13
  N4: R2.Pin_1, LED1.anode, J1.pin2
  N5: Mod1.pin_18, Mod1.pin_19

custom parts:
  deneyap kart: deneyap kart ESP development board.
